# Fritzing sketch Example setup (saved by Fritzing 0.9.3b)
breadboards: 1

parts:
  VCC1 = Battery
  R1 = Resistor [tolerance=±5% resistance=220 package=THT]
  R2 = Resistor [tolerance=±5% resistance=220 package=THT]
  Ohmmeter1 = Ohmmeter
  Amperemeter1 = Amperemeter
  Voltmeter1 = Voltmeter

nets:
  N1: VCC1.-, R2.Pin_1, Voltmeter1.COM
  N2: VCC1.+, Amperemeter1.Input, Voltmeter1.Input
  N3: R1.Pin_0, Ohmmeter1.Input
  N4: R1.Pin_1, Ohmmeter1.COM
  N5: R2.Pin_0, Amperemeter1.COM

custom parts:
  Ohmmeter: Analog Ohmmeter based on PeakTech 3201
  Amperemeter: Analog Multimeter, drawing based on PeakTech 3201
  Voltmeter: Analog Multimeter based on PeakTech 3201
