# Fritzing sketch Example setup (saved by Fritzing 0.9.3b)
breadboards: 1

parts:
  Amperemeter1 = Amperemeter
  Ohmmeter1 = Ohmmeter
  Voltmeter1 = Voltmeter
  VCC1 = Battery
  R1 = Resistor [tolerance=±5% resistance=220 package=THT]
  R2 = Resistor [tolerance=±5% resistance=220 package=THT]

nets:
  N1: Amperemeter1.COM, R2.Pin_0
  N2: Amperemeter1.Input, Voltmeter1.Input, VCC1.+
  N3: Ohmmeter1.COM, R1.Pin_1
  N4: Ohmmeter1.Input, R1.Pin_0
  N5: Voltmeter1.COM, VCC1.-, R2.Pin_1

custom parts:
  Amperemeter: Digital Multimeter, drawing based on PeakTech 3340
  Ohmmeter: Digital Multimeter, drawing based on PeakTech 3340
  Voltmeter: Digital Multimeter, drawing based on PeakTech 3340
